// Logisim project cpu.circ as structural Verilog: 1 circuit, main circuit cpu
module cpu (
  input  Rest
);

  wire Clk_out;
  wire [31:0] adder_1_out, PC_q, RegisterFile_p1, RegisterFile_p2, RegisterFile_p3;

  Clock Clk (.out(Clk_out));
  Register #(.width(32)) PC (.D(adder_1_out), .en(1'b1), .clk(Clk_out), .Q(PC_q), .clr(Rest));
  Adder #(.width(32)) adder_1 (.a(32'h4), .b(PC_q), .out(adder_1_out));  // open: cin, cout
  mem InstMem (.MemAddress(PC_q), .clk(Clk_out));  // open: MemWriteMask, MemWriteData, MemReadData
  // regfile RegisterFile: pin names not known; wires that end beside it: RegisterFile_p1, RegisterFile_p2, RegisterFile_p3
  ALU alu_1 (
    .ReadData1(RegisterFile_p2), .ReadData2(RegisterFile_p3), .Result(RegisterFile_p1));  // open: ControlBits, Zero
  // mem DataMem: pin names not known
endmodule
